# Fritzing sketch walvola04 (saved by Fritzing 0.9.3b)
circuit board: 4.4cm x 4.8cm
breadboards: 1

parts:
  R1 = Resistor [tolerance=±5% resistance=10k package=THT]
  R2 = Resistor [tolerance=±5% resistance=10k package=THT]
  ESP = ESP8266 WiFi Module [part_number=ESP8266]
  R3 = Resistor [tolerance=±5% resistance=10k package=THT]
  R4 = Resistor [tolerance=±5% resistance=10k package=THT]
  M+ = Header 1 [package=1x01_offset]
  M- = Header 1 [package=1x01_offset]
  GND = Header 1 [package=1x01_offset]
  VCC = Header 1 [package=1x01_offset]
  Q1 = PNP-Transistor [package="TO92 [THT]"]
  Q2 = NPN-Transistor [package="TO92 [THT]"]
  Q3 = NPN-Transistor [package="TO92 [THT]"]
  Q4 = PNP-Transistor [package="TO92 [THT]"]
  Q5 = NPN-Transistor [package="TO92 [THT]"]
  Q6 = NPN-Transistor [package="TO92 [THT]"]
  C2 = Ceramic Capacitor [capacitance="100 nF" package="200 mil [THT, multilayer]"]

nets:
  N1: R1.Pin_0, ESP.GPIO_4
  N2: R1.Pin_1, Q2.B
  N3: R2.Pin_0, Q5.B
  N4: R2.Pin_1, ESP.GPIO_5
  N5: ESP.VCC, ESP.GPIO_2, ESP.CH_PD, R3.Pin_1, R4.Pin_0, VCC.1, Q1.E, Q4.E, C2.1
  N6: ESP.GPIO_0, R3.Pin_0
  N7: ESP.GND, ESP.GPIO_15, GND.1, Q3.E, Q6.E, C2.0
  N8: ESP.GPIO_16, ESP.REST, R4.Pin_1
  N9: M+.1, Q1.C, Q3.C
  N10: M-.1, Q4.C, Q6.C
  N11: Q1.B, Q2.C
  N12: Q2.E, Q6.B
  N13: Q3.B, Q5.E
  N14: Q4.B, Q5.C
