# Fritzing sketch walvola05 (saved by Fritzing 0.9.3b)
circuit board: 4.4cm x 4.8cm
breadboards: 1

parts:
  R1 = Resistor [tolerance=±5% resistance=10k package=THT]
  R2 = Resistor [tolerance=±5% resistance=10k package=THT]
  ESP = ESP8266 WiFi Module [part_number=ESP8266]
  R3 = Resistor [tolerance=±5% resistance=10k package=THT]
  R4 = Resistor [tolerance=±5% resistance=10k package=THT]
  M+ = Header 1 [package=1x01_offset]
  M- = Header 1 [package=1x01_offset]
  GND = Header 1 [package=1x01_offset]
  VCC = Header 1 [package=1x01_offset]
  Q1 = PNP-Transistor [package="TO92 [THT]"]
  Q2 = NPN-Transistor [package="TO92 [THT]"]
  Q3 = NPN-Transistor [package="TO92 [THT]"]
  Q4 = PNP-Transistor [package="TO92 [THT]"]
  Q5 = NPN-Transistor [package="TO92 [THT]"]
  Q6 = NPN-Transistor [package="TO92 [THT]"]
  C3 = Capacitor Polarized [package=cpol-radial-10uf-25v]
  R5 = Resistor [tolerance=±5% resistance=10k package=THT]
  R6 = Resistor [tolerance=±5% resistance=10k package=THT]
  R7 = Resistor [tolerance=±5% resistance=10k package=THT]
  R8 = Resistor [tolerance=±5% resistance=470 package=THT]
  C5 = Ceramic Capacitor [capacitance=1pF package="200 mil [THT, multilayer]"]

nets:
  N1: R1.Pin_0, ESP.GPIO_4
  N2: R1.Pin_1, Q2.B
  N3: R2.Pin_0, Q5.B
  N4: R2.Pin_1, ESP.GPIO_5
  N5: ESP.VCC, R3.Pin_1, R4.Pin_0, VCC.1, Q1.E, Q4.E, C3.+, R6.Pin_0, R7.Pin_1
  N6: ESP.GPIO_0, R3.Pin_0
  N7: ESP.GPIO_2, R6.Pin_1
  N8: ESP.CH_PD, R7.Pin_0
  N9: ESP.GND, GND.1, Q3.E, Q6.E, C3.-, R5.Pin_1, C5.0
  N10: ESP.GPIO_15, R5.Pin_0
  N11: ESP.GPIO_16, R8.Pin_0
  N12: ESP.REST, R4.Pin_1, R8.Pin_1, C5.1
  N13: M+.1, Q1.C, Q3.C
  N14: M-.1, Q4.C, Q6.C
  N15: Q1.B, Q2.C
  N16: Q2.E, Q6.B
  N17: Q3.B, Q5.E
  N18: Q4.B, Q5.C
